// Logisim project proj4.circ as structural Verilog: 13 circuits, main circuit main
module main (
  input  [2:0] Control,
  input  [7:0] A,
  input  [7:0] B,
  output [7:0] Result,
  output Zero,
  output Negative,
  output Carry,
  output Overflow
);

  wire or_1_out;
  wire [7:0] ADD_result, n8_bit_and_1_result, n8_bit_div_1_out_3, n8_bit_mul_1_out_3, n8_bit_or_1_result,
       n8_bit_shl_1_out_3, n8_bit_shr_1_out_3, SUB_result;

  _8_bit_AND u_8_bit_and_1 (.Result(n8_bit_and_1_result), .A(A), .B(B));
  _8_bit_OR u_8_bit_or_1 (.Result(n8_bit_or_1_result), .A(A), .B(B));
  _8_bit_Adder_Subtracter ADD (
    .Add_Sub_Control(1'b0), .Result(ADD_result), .A(A), .B(B), .Carry_out(Carry), .Overflow(Overflow));
  _8_bit_Adder_Subtracter SUB (.Add_Sub_Control(1'b1), .Result(SUB_result), .A(A), .B(B));  // open: Carry_out, Overflow
  _8_bit_shl u_8_bit_shl_1 (.Number(A), .Shift_by(B), .out_3(n8_bit_shl_1_out_3));
  _8_bit_shr u_8_bit_shr_1 (.Number(A), .Shift_by(B), .out_3(n8_bit_shr_1_out_3));
  _8_bit_mul u_8_bit_mul_1 (.A(A), .B(B), .out_3(n8_bit_mul_1_out_3));
  _8_bit_div u_8_bit_div_1 (.A(A), .B(B), .out_3(n8_bit_div_1_out_3));
  _8_bit_8x1_mux u_8_bit_8x1_mux_1 (
    .D1(n8_bit_and_1_result), .D2(n8_bit_or_1_result), .D3(ADD_result), .D4(SUB_result),
    .D5(n8_bit_shl_1_out_3), .D6(n8_bit_shr_1_out_3), .D7(n8_bit_mul_1_out_3), .D8(n8_bit_div_1_out_3),
    .Selector(Control), .Output({Negative, Result[6:0]}));
  or or_1 (or_1_out, Result[0], Result[1], Result[2], Result[3], Result[4], Result[5], Result[6], Negative);
  not not_1 (Zero, or_1_out);

  assign Result[7] = Negative;

  // Notes on the sheet:
  //   AND
  //   OR
  //   Full 8-bit ALU
endmodule

// +
module _1_bit_Adder (
  input  Carry_In,
  input  A,
  input  B,
  output Result,
  output Carry_Out
);

  wire and_1_out, and_2_out, xor_1_out;

  and and_1 (and_1_out, A, B);
  xor xor_1 (xor_1_out, A, B);
  or or_1 (Carry_Out, and_1_out, and_2_out);
  and and_2 (and_2_out, Carry_In, xor_1_out);
  xor xor_2 (Result, Carry_In, xor_1_out);

  // Notes on the sheet:
  //   Full Adder
endmodule

// +/-
module _8_bit_Adder_Subtracter (
  input  Add_Sub_Control,
  input  [7:0] A,
  input  [7:0] B,
  output [7:0] Result,
  output Carry_out,
  output Overflow
);

  wire and_1_out, and_2_out, n1_bit_adder_1_carry_out, n1_bit_adder_2_carry_out, n1_bit_adder_3_carry_out,
       n1_bit_adder_4_carry_out, n1_bit_adder_5_carry_out, n1_bit_adder_6_carry_out,
       n1_bit_adder_7_carry_out, not_1_out, not_2_out, not_3_out, xor_1_out, xor_2_out, xor_3_out, xor_4_out,
       xor_5_out, xor_6_out, xor_7_out, xor_8_out;

  xor xor_1 (xor_1_out, Add_Sub_Control, B[0]);
  xor xor_2 (xor_2_out, Add_Sub_Control, B[1]);
  xor xor_3 (xor_3_out, Add_Sub_Control, B[2]);
  xor xor_4 (xor_4_out, Add_Sub_Control, B[3]);
  xor xor_5 (xor_5_out, Add_Sub_Control, B[4]);
  xor xor_6 (xor_6_out, Add_Sub_Control, B[5]);
  xor xor_7 (xor_7_out, Add_Sub_Control, B[6]);
  xor xor_8 (xor_8_out, Add_Sub_Control, B[7]);
  not not_1 (not_1_out, xor_8_out);
  not not_2 (not_2_out, A[7]);
  _1_bit_Adder u_1_bit_adder_1 (
    .A(A[0]), .B(xor_1_out), .Result(Result[0]), .Carry_Out(n1_bit_adder_1_carry_out),
    .Carry_In(Add_Sub_Control));
  _1_bit_Adder u_1_bit_adder_2 (
    .A(A[1]), .B(xor_2_out), .Result(Result[1]), .Carry_Out(n1_bit_adder_2_carry_out),
    .Carry_In(n1_bit_adder_1_carry_out));
  _1_bit_Adder u_1_bit_adder_3 (
    .A(A[2]), .B(xor_3_out), .Result(Result[2]), .Carry_Out(n1_bit_adder_3_carry_out),
    .Carry_In(n1_bit_adder_2_carry_out));
  _1_bit_Adder u_1_bit_adder_4 (
    .A(A[3]), .B(xor_4_out), .Result(Result[3]), .Carry_Out(n1_bit_adder_4_carry_out),
    .Carry_In(n1_bit_adder_3_carry_out));
  _1_bit_Adder u_1_bit_adder_5 (
    .A(A[4]), .B(xor_5_out), .Result(Result[4]), .Carry_Out(n1_bit_adder_5_carry_out),
    .Carry_In(n1_bit_adder_4_carry_out));
  _1_bit_Adder u_1_bit_adder_6 (
    .A(A[5]), .B(xor_6_out), .Result(Result[5]), .Carry_Out(n1_bit_adder_6_carry_out),
    .Carry_In(n1_bit_adder_5_carry_out));
  _1_bit_Adder u_1_bit_adder_7 (
    .A(A[6]), .B(xor_7_out), .Result(Result[6]), .Carry_Out(n1_bit_adder_7_carry_out),
    .Carry_In(n1_bit_adder_6_carry_out));
  _1_bit_Adder u_1_bit_adder_8 (
    .A(A[7]), .B(xor_8_out), .Result(Result[7]), .Carry_Out(Carry_out), .Carry_In(n1_bit_adder_7_carry_out));
  not not_3 (not_3_out, Result[7]);
  and and_1 (and_1_out, Result[7], not_2_out, not_1_out);
  and and_2 (and_2_out, not_3_out, A[7], xor_8_out);
  or or_1 (Overflow, and_1_out, and_2_out);

  // Notes on the sheet:
  //   8-bit Adder/Subtractor
endmodule

module _8_bit_AND (
  input  [7:0] A,
  input  [7:0] B,
  output [7:0] Result
);

  and AND (Result[0], A[0], B[0]);
  and AND_2 (Result[1], A[1], B[1]);
  and AND_3 (Result[2], A[2], B[2]);
  and AND_4 (Result[3], A[3], B[3]);
  and AND_5 (Result[4], A[4], B[4]);
  and AND_6 (Result[5], A[5], B[5]);
  and AND_7 (Result[6], A[6], B[6]);
  and AND_8 (Result[7], A[7], B[7]);

  // Notes on the sheet:
  //   8-bit AND
endmodule

module _8_bit_OR (
  input  [7:0] A,
  input  [7:0] B,
  output [7:0] Result
);

  or OR (Result[0], A[0], B[0]);
  or OR_2 (Result[1], A[1], B[1]);
  or OR_3 (Result[2], A[2], B[2]);
  or OR_4 (Result[3], A[3], B[3]);
  or OR_5 (Result[4], A[4], B[4]);
  or OR_6 (Result[5], A[5], B[5]);
  or OR_7 (Result[6], A[6], B[6]);
  or OR_8 (Result[7], A[7], B[7]);

  // Notes on the sheet:
  //   8-bit OR
endmodule

module _8_bit_mux (
  input  Control_Pin,
  input  [7:0] A,
  input  [7:0] B,
  output [7:0] Output
);
endmodule

module _8_bit_8x1_mux (
  input  [2:0] Selector,
  input  [7:0] D1,
  input  [7:0] D2,
  input  [7:0] D3,
  input  [7:0] D4,
  input  [7:0] D5,
  input  [7:0] D6,
  input  [7:0] D7,
  input  [7:0] D8,
  output [7:0] Output
);

  _1_bit_8x1_mux BIT_0 (
    .D1(D1[0]), .D2(D2[0]), .D3(D3[0]), .D4(D4[0]), .D5(D5[0]), .D6(D6[0]), .D7(D7[0]), .D8(D8[0]),
    .S1(Selector), .Output(Output[0]));
  _1_bit_8x1_mux BIT_1 (
    .D1(D1[1]), .D2(D2[1]), .D3(D3[1]), .D4(D4[1]), .D5(D5[1]), .D6(D6[1]), .D7(D7[1]), .D8(D8[1]),
    .S1(Selector), .Output(Output[1]));
  _1_bit_8x1_mux Bit_2 (
    .D1(D1[2]), .D2(D2[2]), .D3(D3[2]), .D4(D4[2]), .D5(D5[2]), .D6(D6[2]), .D7(D7[2]), .D8(D8[2]),
    .S1(Selector), .Output(Output[2]));
  _1_bit_8x1_mux Bit_3 (
    .D1(D1[3]), .D2(D2[3]), .D3(D3[3]), .D4(D4[3]), .D5(D5[3]), .D6(D6[3]), .D7(D7[3]), .D8(D8[3]),
    .S1(Selector), .Output(Output[3]));
  _1_bit_8x1_mux u_1_bit_8x1_mux_1 (
    .D1(D1[4]), .D2(D2[4]), .D3(D3[4]), .D4(D4[4]), .D5(D5[4]), .D6(D6[4]), .D7(D7[4]), .D8(D8[4]),
    .S1(Selector), .Output(Output[4]));
  _1_bit_8x1_mux u_1_bit_8x1_mux_2 (
    .D1(D1[5]), .D2(D2[5]), .D3(D3[5]), .D4(D4[5]), .D5(D5[5]), .D6(D6[5]), .D7(D7[5]), .D8(D8[5]),
    .S1(Selector), .Output(Output[5]));
  _1_bit_8x1_mux u_1_bit_8x1_mux_3 (
    .D1(D1[6]), .D2(D2[6]), .D3(D3[6]), .D4(D4[6]), .D5(D5[6]), .D6(D6[6]), .D7(D7[6]), .D8(D8[6]),
    .S1(Selector), .Output(Output[6]));
  _1_bit_8x1_mux u_1_bit_8x1_mux_4 (
    .D1(D1[7]), .D2(D2[7]), .D3(D3[7]), .D4(D4[7]), .D5(D5[7]), .D6(D6[7]), .D7(D7[7]), .D8(D8[7]),
    .S1(Selector), .Output(Output[7]));
endmodule

// 8x1 MUX
module _1_bit_8x1_mux (
  input  [2:0] S1,
  input  D1,
  input  D2,
  input  D3,
  input  D4,
  input  D5,
  input  D6,
  input  D7,
  input  D8,
  output Output
);

  wire and_1_out, and_2_out, and_3_out, and_4_out, and_5_out, and_6_out, and_7_out, and_8_out, not_1_out,
       not_2_out, not_3_out, or_1_out, or_2_out;

  not not_1 (not_1_out, S1[2]);
  not not_2 (not_2_out, S1[1]);
  not not_3 (not_3_out, S1[0]);
  and and_1 (and_1_out, D1, not_3_out, not_2_out, not_1_out);
  and and_2 (and_2_out, D2, S1[0], not_2_out, not_1_out);
  and and_3 (and_3_out, D3, not_3_out, S1[1], not_1_out);
  and and_4 (and_4_out, D4, S1[0], S1[1], not_1_out);
  and and_5 (and_5_out, D5, not_3_out, not_2_out, S1[2]);
  and and_6 (and_6_out, D6, S1[0], not_2_out, S1[2]);
  and and_7 (and_7_out, D7, not_3_out, S1[1], S1[2]);
  and and_8 (and_8_out, D8, S1[0], S1[1], S1[2]);
  or or_1 (or_1_out, and_1_out, and_2_out, and_3_out, and_4_out);
  or or_2 (or_2_out, and_5_out, and_6_out, and_7_out, and_8_out);
  or or_3 (Output, or_1_out, or_2_out);
endmodule

module _8_bit_8x1_testing (
  input  [2:0] Selector,
  input  [7:0] D1,
  input  [7:0] D2,
  input  [7:0] D3,
  input  [7:0] D4,
  input  [7:0] D5,
  input  [7:0] D6,
  input  [7:0] D7,
  input  [7:0] D8,
  output [7:0] Output
);

  _8_bit_8x1_mux u_8_bit_8x1_mux_1 (
    .D1(D1), .D2(D2), .D3(D3), .D4(D4), .D5(D5), .D6(D6), .D7(D7), .D8(D8), .Selector(Selector),
    .Output(Output));
endmodule

// SHL
module _8_bit_shl (
  input  [7:0] Number,
  input  [7:0] Shift_by,
  output [7:0] out_3
);
endmodule

// SHR
module _8_bit_shr (
  input  [7:0] Number,
  input  [7:0] Shift_by,
  output [7:0] out_3
);
endmodule

// MUL
module _8_bit_mul (
  input  [7:0] A,
  input  [7:0] B,
  output [7:0] out_3
);
endmodule

// DIV
module _8_bit_div (
  input  [7:0] A,
  input  [7:0] B,
  output [7:0] out_3
);
endmodule
